// Logisim project trab.circ as structural Verilog: 2 circuits, main circuit main
module main (
  input  [7:0] in_1
);

  wire and_1_out, and_2_out, and_3_out, and_4_out, and_5_out, button_1_out, clk, MOV, not_1_out, not_2_out,
       not_3_out, not_4_out, not_5_out, not_6_out;
  wire [1:0] RAMADDR, REGADDR;
  wire [4:0] counter_1_q;
  wire [7:0] controlled_buffer_4_out, controlled_buffer_5_out, controlled_buffer_6_out,
       controlled_buffer_7_out, ram_1_data, RAMOUT, rom_1_data;

  not not_1 (not_1_out, clk);
  Clock clock_1 (.out(clk));
  Counter #(.width(5), .max('h1f)) counter_1 (
    .Q(counter_1_q), .clk(clk), .clr(button_1_out));  // open: load, D, count, carry
  Button button_1 (.out(button_1_out));
  RAM #(.addrWidth(2), .bus("asynch")) ram_1 (.addr(RAMADDR), .data(ram_1_data), .ld(not_1_out));  // open: sel, clr
  not not_2 (not_2_out, clk);
  assign RAMOUT = not_2_out ? ram_1_data : 8'bz;  // Controlled_Buffer controlled_buffer_1
  assign ram_1_data = clk ? in_1 : 8'bz;  // Controlled_Buffer controlled_buffer_2
  ROM #(.addrWidth(5)) rom_1 (.addr(counter_1_q), .data(rom_1_data));  // open: sel
  assign RAMOUT = clk ? {8{1'b0}} : 8'bz;  // Controlled_Buffer controlled_buffer_3
  assign controlled_buffer_4_out = and_1_out ? RAMOUT : 8'bz;  // Controlled_Buffer controlled_buffer_4
  Register register_1 (.D(controlled_buffer_4_out), .clk(clk));  // open: en, Q, clr
  instr_dec instr_dec_1 (.INSTR(rom_1_data), .RDM(MOV), .REGADDR(REGADDR), .RAMADDR(RAMADDR));
  not not_3 (not_3_out, REGADDR[1]);
  not not_4 (not_4_out, REGADDR[0]);
  assign controlled_buffer_5_out = and_2_out ? RAMOUT : 8'bz;  // Controlled_Buffer controlled_buffer_5
  and and_1 (and_1_out, not_3_out, not_4_out);
  Register register_2 (.D(controlled_buffer_5_out), .clk(clk));  // open: en, Q, clr
  and and_2 (and_2_out, REGADDR[0], not_5_out);
  not not_5 (not_5_out, REGADDR[1]);
  not not_6 (not_6_out, REGADDR[0]);
  assign controlled_buffer_6_out = and_4_out ? RAMOUT : 8'bz;  // Controlled_Buffer controlled_buffer_6
  Register register_3 (.D(controlled_buffer_6_out), .clk(clk));  // open: en, Q, clr
  and and_3 (and_3_out, MOV, REGADDR[1]);
  and and_4 (and_4_out, not_6_out, REGADDR[1]);
  and and_5 (and_5_out, and_3_out, REGADDR[0]);
  assign controlled_buffer_7_out = and_5_out ? RAMOUT : 8'bz;  // Controlled_Buffer controlled_buffer_7
  Register register_4 (.D(controlled_buffer_7_out), .clk(clk));  // open: en, Q, clr

  // Other names for the same wires on the sheet: RAMIN[7:0] = in_1

  // Notes on the sheet:
  //   contents of rom_1 (hex, n*v repeats v):
  //   de 2 3 4 d0 d1 d2 d3 df e0
endmodule

module instr_dec (
  input  [7:0] INSTR,
  output RDM,
  output [1:0] REGADDR,
  output [1:0] RAMADDR
);

  wire and_1_out, and_2_out, not_1_out;

  and and_1 (and_1_out, INSTR[7], INSTR[6]);
  not not_1 (not_1_out, INSTR[5]);
  and and_2 (and_2_out, and_1_out, not_1_out);
  and and_3 (RDM, and_2_out, INSTR[4]);
  assign REGADDR = RDM ? INSTR[3:2] : 2'bz;  // Controlled_Buffer controlled_buffer_1
  assign RAMADDR = RDM ? INSTR[1:0] : 2'bz;  // Controlled_Buffer controlled_buffer_2
endmodule
